// Logisim project schemes.circ as structural Verilog: 1 circuit, main circuit DataPath
module DataPath (
  input  in_1,
  input  in_2,
  input  in_3,
  input  in_4,
  input  in_5,
  input  in_6,
  input  in_7,
  input  in_8,
  input  in_9,
  input  in_10,
  input  in_11,
  input  in_12,
  input  in_13,
  input  in_14,
  input  in_15,
  input  in_16,
  input  in_17,
  input  in_18,
  input  in_19,
  input  in_20,
  input  in_21,
  input  in_22,
  input  in_23,
  input  in_24,
  input  in_25,
  input  in_26,
  input  in_27,
  input  in_28,
  input  in_29,
  input  [3:0] in_30,
  input  [2:0] in_31,
  input  in_32,
  input  in_33,
  output [2:0] out_34
);

  wire and_1_out, or_1_out;
  wire [2:0] comparator_1_lt;
  wire [31:0] adder_1_out, and_2_out, controlled_buffer_1_out, controlled_buffer_2_out, multiplexer_1_out,
       multiplexer_2_out, not_1_out, register_1_q, register_2_q, register_3_q, register_4_q, register_5_q,
       register_6_q, register_7_q, register_8_q, register_9_q, register_10_q, register_11_q, register_12_q,
       register_13_q, register_14_q, register_15_q, register_16_q, register_18_q, register_19_q,
       register_20_q, register_21_q, shifter_1_out, shifter_2_out;

  Register #(.width(32)) register_1 (.D(controlled_buffer_2_out), .Q(register_1_q), .clk(in_4));  // open: en, clr
  Register #(.width(32)) register_2 (.D(controlled_buffer_2_out), .Q(register_2_q), .clk(in_9));  // open: en, clr
  Register #(.width(32)) register_3 (.D(controlled_buffer_2_out), .Q(register_3_q), .clk(in_13));  // open: en, clr
  Register #(.width(32)) register_4 (.D(controlled_buffer_2_out), .Q(register_4_q), .clk(in_15));  // open: en, clr
  Register #(.width(32)) register_5 (.D(controlled_buffer_2_out), .Q(register_5_q), .clk(in_19));  // open: en, clr
  Register #(.width(32)) register_6 (.D(controlled_buffer_2_out), .Q(register_6_q), .clk(in_22));  // open: en, clr
  Register #(.width(32)) register_7 (.D(controlled_buffer_2_out), .Q(register_7_q), .clk(in_24));  // open: en, clr
  Register #(.width(32)) register_8 (.D(controlled_buffer_2_out), .Q(register_8_q), .clk(in_28));  // open: en, clr
  Register #(.width(32)) register_9 (.D(controlled_buffer_2_out), .Q(register_9_q), .clk(in_5));  // open: en, clr
  Register #(.width(32)) register_10 (.D(controlled_buffer_2_out), .Q(register_10_q), .clk(in_10));  // open: en, clr
  Register #(.width(32)) register_11 (.D(controlled_buffer_2_out), .Q(register_11_q), .clk(in_14));  // open: en, clr
  Register #(.width(32)) register_12 (.D(controlled_buffer_2_out), .Q(register_12_q), .clk(in_16));  // open: en, clr
  Register #(.width(32)) register_13 (.D(controlled_buffer_2_out), .Q(register_13_q), .clk(in_20));  // open: en, clr
  Register #(.width(32)) register_14 (.D(controlled_buffer_2_out), .Q(register_14_q), .clk(in_23));  // open: en, clr
  Register #(.width(32)) register_15 (.D(controlled_buffer_2_out), .Q(register_15_q), .clk(in_25));  // open: en, clr
  Register #(.width(32)) register_16 (.D(controlled_buffer_2_out), .Q(register_16_q), .clk(in_29));  // open: en, clr
  Multiplexer #(.select(4), .width(32)) multiplexer_1 (
    .in0(register_1_q), .in1(register_2_q), .in2(register_3_q), .in3(register_4_q), .in4(register_9_q),
    .in5(register_10_q), .in6(register_11_q), .in7(register_12_q), .in8(register_13_q), .in9(register_14_q),
    .in10(register_15_q), .in11(register_16_q), .in12(register_5_q), .in13(register_6_q),
    .in14(register_7_q), .in15(register_8_q), .out(multiplexer_1_out), .sel(in_30));  // open: en
  Register #(.width(3)) register_17 (.D(comparator_1_lt), .Q(out_34), .clk(in_33));  // open: en, clr
  Register #(.width(32)) register_18 (
    .D(controlled_buffer_2_out), .Q(register_18_q), .clk(in_1), .clr(in_2));  // open: en
  Register #(.width(32)) register_19 (
    .D(controlled_buffer_2_out), .Q(register_19_q), .clk(in_11), .clr(in_12));  // open: en
  and and_1 (and_1_out, in_26, out_34[2]);
  Register #(.width(32)) register_20 (.D(multiplexer_1_out), .Q(register_20_q), .clk(in_17), .clr(in_18));  // open: en
  or or_1 (or_1_out, in_21, and_1_out);
  assign controlled_buffer_1_out = in_8 ? register_19_q : 32'bz;  // Controlled_Buffer controlled_buffer_1
  assign controlled_buffer_2_out = in_7 ? controlled_buffer_1_out : 32'bz;  // Controlled_Buffer controlled_buffer_2
  assign and_2_out = register_20_q & register_19_q;  // AND_Gate and_2, 32 bits wide
  assign not_1_out = ~register_19_q;  // NOT_Gate not_1, 32 bits wide
  Adder #(.width(32)) adder_1 (
    .a(register_20_q), .b(register_19_q), .out(adder_1_out), .cin(or_1_out), .cout(comparator_1_lt[2]));
  Shifter #(.width(32)) shifter_1 (.in(register_20_q), .\dist (register_19_q[4:0]), .out(shifter_1_out));
  Shifter #(.width(32), .shift("lr")) shifter_2 (.in(register_20_q), .\dist (register_19_q[4:0]), .out(shifter_2_out));
  RAM #(.addrWidth(24), .dataWidth(32)) ram_1 (
    .addr(register_18_q[23:0]), .data(controlled_buffer_1_out), .sel(in_3), .clk(in_6), .ld(in_7));  // open: clr
  Multiplexer #(.select(3), .width(32)) multiplexer_2 (
    .in0(and_2_out), .in1(not_1_out), .in2(adder_1_out), .in3(shifter_1_out), .in4(shifter_2_out),
    .in5({{16{1'b0}}, register_19_q[15:0]}), .out(multiplexer_2_out), .sel(in_31));  // open: in6, in7, en
  Comparator #(.width(32)) comparator_1 (
    .a(multiplexer_2_out), .b({32{1'b0}}), .eq(comparator_1_lt[1]), .lt(comparator_1_lt[0]));  // open: gt
  Register #(.width(32)) register_21 (.D(multiplexer_2_out), .Q(register_21_q), .clk(in_32));  // open: en, clr
  assign controlled_buffer_2_out = in_27 ? register_21_q : 32'bz;  // Controlled_Buffer controlled_buffer_3
endmodule
